# Fritzing sketch schematic (saved by Fritzing 0.9.4)
breadboards: 1

parts:
  Part1 = Arduino Uno (Rev3)
  U1 = ESP8266 WiFi Module [part_number=ESP8266]
  R1 = Resistor [tolerance=±5% resistance=10k package=THT]
  R2 = Resistor [tolerance=±5% resistance=1k package=THT]
  R3 = Resistor [tolerance=±5% resistance=2k package=THT]
  U2 = 2-Channel 5v Relay Shield [package=relay-2ch5v10a]
  M1 = DC Motor
  HLK-PM1 = HLK-PM12 [part_number=HLK-PM12]

nets (from the breadboard view):
  N1: Part1.D8, U2.IN2
  GND: Part1.GND, U1.GND, R3.Pin_0, U2.GND
  N2: Part1.D2, U1.TXD
  N3: Part1.D3_PWM, R2.Pin_0
  N4: Part1.D7, U2.IN1
  3V3: Part1.3V3, U1.VCC, R1.Pin_0
  5V: Part1.5V, U2.VCC
  N5: U1.RXD, R2.Pin_1, R3.Pin_1
  N6: U1.CH_PD, R1.Pin_1
  N7: U2.K1-In, M1.pin_1
  N8: U2.K1-Off, U2.K2-Off, HLK-PM1.+Vo
  N9: U2.K1-On, U2.K2-On, HLK-PM1.-Vo
  N10: U2.K2-In, M1.pin_2

notes:
  By Kyle Thai

custom parts:
  ESP8266 WiFi Module: Generic WiFi Module based on the ESP8266 with onboard PCB antenna and UART communications
  2-Channel 5v Relay Shield: 2 Channel 5v Relay Shield w. 2x SPD-06VDC-SD-C
